# Fritzing sketch sketch (saved by Fritzing 0.9.4)

parts:
  Raspberry_Pi1 = Raspberry Pi B+
  Part3 = I2C level shifter bidirectional
  LCD1 = LCD screen
  LCM1602_IIC1 = LCM1602 IIC [part_number="LCM1602 IIC" chip_label="LCM1602 IIC" package="DIP (Dual Inline) [THT]"]

nets:
  N1: Raspberry_Pi1.3v3, Part3.LV
  N2: Raspberry_Pi1.GPIO2, Part3.LV1
  N3: Raspberry_Pi1.GPIO3, Part3.LV2
  GND: Raspberry_Pi1.GND, Part3.GND, LCM1602_IIC1.GND
  5V: Raspberry_Pi1.5V, Part3.HV, LCM1602_IIC1.VCC
  N4: Part3.HV1, LCM1602_IIC1.SDA
  N5: Part3.HV2, LCM1602_IIC1.SCL
  VSS: LCD1.VSS, LCM1602_IIC1.VSS
  VDD: LCD1.VDD, LCM1602_IIC1.VDD
  N6: LCD1.V0, LCM1602_IIC1.V0
  N7: LCD1.RS, LCM1602_IIC1.RS
  N8: LCD1.R/W, LCM1602_IIC1.RW
  N9: LCD1.E, LCM1602_IIC1.E
  N10: LCD1.DB0, LCM1602_IIC1.D0
  N11: LCD1.DB1, LCM1602_IIC1.D1
  N12: LCD1.DB2, LCM1602_IIC1.D2
  N13: LCD1.DB3, LCM1602_IIC1.D3
  N14: LCD1.DB4, LCM1602_IIC1.D4
  N15: LCD1.DB5, LCM1602_IIC1.D5
  N16: LCD1.DB6, LCM1602_IIC1.D6
  N17: LCD1.DB7, LCM1602_IIC1.D7
  N18: LCD1.LED+, LCM1602_IIC1.A
  N19: LCD1.LED-, LCM1602_IIC1.K

custom parts:
  LCM1602 IIC: I2C-Module to use a 1602 or 2004 LCD on with the wire.h libory Serial LCD Modul
